// Logisim project lab1.circ as structural Verilog
module \一位二进制半加器  (
  input  A,
  input  B,
  output \本位和S ,
  output \进位C 
);

  xor xor_1 (\本位和S , A, B);
  and and_1 (\进位C , A, B);
endmodule

module \一位二进制全加器  (
  input  A,
  input  B,
  input  Ci,
  output \本位和S ,
  output Co
);

  wire and_1_out, and_2_out, xor_2_out;

  xor xor_1 (\本位和S , xor_2_out, Ci);
  xor xor_2 (xor_2_out, A, B);
  or or_1 (Co, and_1_out, and_2_out);
  and and_1 (and_1_out, xor_2_out, Ci);
  and and_2 (and_2_out, A, B);
endmodule

module \四位二进制串行加法器  (
  input  A3,
  input  A2,
  input  A1,
  input  A0,
  input  B3,
  input  B2,
  input  B1,
  input  B0,
  input  C0,
  output S3,
  output S2,
  output S1,
  output S0,
  output C4
);

  wire \一位二进制全加器_2_co , \一位二进制全加器_3_co , \一位二进制全加器_4_co ;

  \一位二进制全加器  \u_一位二进制全加器_1  (.\本位和S (S3), .Co(C4), .A(A3), .B(B3), .Ci(\一位二进制全加器_2_co ));
  \一位二进制全加器  \u_一位二进制全加器_2  (.\本位和S (S2), .Co(\一位二进制全加器_2_co ), .A(A2), .B(B2), .Ci(\一位二进制全加器_3_co ));
  \一位二进制全加器  \u_一位二进制全加器_3  (.\本位和S (S1), .Co(\一位二进制全加器_3_co ), .A(A1), .B(B1), .Ci(\一位二进制全加器_4_co ));
  \一位二进制全加器  \u_一位二进制全加器_4  (.\本位和S (S0), .Co(\一位二进制全加器_4_co ), .A(A0), .B(B0), .Ci(C0));
endmodule
